# Fritzing sketch ElbanquosKitchentimer_MK1 (saved by Fritzing 0.9.3b)
breadboards: 2

parts:
  S1 = Pushbutton [package="[THT]"]  # not connected
  S2 = Pushbutton [package="[THT]"]  # not connected
  S3 = Pushbutton [package="[THT]"]  # not connected
  S4 = Pushbutton [package="[THT]"]  # not connected
  LED1 = smd LED [color="Red (633nm)" package="1206 [SMD]"]  # not connected
  LED2 = smd LED [color="Red (633nm)" package="1206 [SMD]"]  # not connected
  LED3 = smd LED [color="Red (633nm)" package="1206 [SMD]"]  # not connected
  LED4 = smd LED [color="Red (633nm)" package="1206 [SMD]"]  # not connected
  TM1638_-_Led_Button_Module = IC, DIP package, 10 pins [chip_label=IC]
  Bauteil1 = Arduino Uno (Rev3)
  RE1 = Rotary Encoder [package=THT]
  Rotary_Button_Function = Pushbutton [package="[THT]"]
  J1 = Piezo Speaker
  R1 = Resistor [tolerance=±5% resistance=560 package=THT]
  VCC1 = Battery block 9V
  J2 = Camdenboss CTB0158-4 [part_number=CTB0158-4 package=THT]
  7_Segment1 = 7 Segment Display  # not connected
  7_Segment2 = 7 Segment Display  # not connected
  7_Segment3 = 7 Segment Display  # not connected
  7_Segment4 = 7 Segment Display  # not connected
  7_Segment5 = 7 Segment Display  # not connected
  7_Segment6 = 7 Segment Display  # not connected
  7_Segment7 = 7 Segment Display  # not connected
  7_Segment8 = 7 Segment Display  # not connected
  R2 = Rotary Potentiometer (Small) [maximum_resistance=100kΩ package=THT]
  R3 = Resistor [tolerance=±5% resistance=4.7k package=THT]
  Q1 = NPN-Transistor [package="TO92 [THT]"]

nets:
  N1: TM1638_-_Led_Button_Module.pin1, Bauteil1.5V
  N2: TM1638_-_Led_Button_Module.pin2, Bauteil1.D4
  N3: TM1638_-_Led_Button_Module.pin3, Bauteil1.D3_PWM
  N4: TM1638_-_Led_Button_Module.pin4, Bauteil1.D2
  N5: TM1638_-_Led_Button_Module.pin5, Bauteil1.GND, RE1.EncoderPinC, Rotary_Button_Function.Pin_3, Rotary_Button_Function.Pin_4, J1.pin2, R1.Pin_1, VCC1.-, J2.pin2, R3.Pin_0
  N6: Bauteil1.D11_PWM/MOSI, Rotary_Button_Function.Pin_1, Rotary_Button_Function.Pin_2
  N7: Bauteil1.D12/MISO, RE1.EncoderPinA
  N8: Bauteil1.D13/SCK, RE1.EncoderPinB
  N9: Bauteil1.D5_PWM, R2.leg2
  N10: Bauteil1.VIN, VCC1.+, J2.pin1, Q1.C
  N11: J1.pin1, R3.Pin_1, Q1.E
  N12: R1.Pin_0, R2.leg1
  N13: R2.wiper, Q1.B

notes:
  Led & Keyboard With
  TM1638
  Some Magic here->
